# Fritzing sketch fan-speed-controller (saved by Fritzing 0.9.9b)
circuit board: 4.18665cm x 4.1994cm
breadboards: 1

parts:
  ATTINY45 = ATTINY45 [package=dip]
  7805 = Voltage Regulator [package=to220-igo]
  1kΩ = Resistor [tolerance=±5% resistance=1k power=0.25 package=THT]
  Terminal_Block = Camdenboss CTB0158-7 [part_number=CTB0158-7 package=THT]
  1kΩ_2 = Resistor [tolerance=±5% resistance=1k power=0.25 package=THT]
  100nf = Ceramic Capacitor [capacitance=100nF voltage=35V package="100 mil [THT, multilayer]"]
  330nf = Ceramic Capacitor [capacitance=0pF voltage=35V package="100 mil [THT, multilayer]"]
  10kΩ = Resistor [tolerance=±5% resistance=10k power=0.25 package=THT]
  220Ω = Resistor [tolerance=±5% resistance=220 power=0.25 package=THT]
  N-FET = Basic FET N-Channel [package="TO220 [THT]"]
  47nf = Ceramic Capacitor [capacitance=100n voltage=35V package="200 mil [THT, multilayer]"]
  10kΩ_2 = Resistor [tolerance=±5% resistance=10k power=0.25 package=THT]
  Z5V = Zener Diode [part_number=1N4732A breakdown_voltage=3.6V package="300 mil [THT]"]
  10kΩ_3 = Resistor [tolerance=±5% resistance=10k power=0.25 package=THT]
  Z5V_2 = Zener Diode [part_number=1N4732A breakdown_voltage=3.6V package="300 mil [THT]"]
  10kΩ_4 = Resistor [tolerance=±5% resistance=10k power=0.25 package=THT]
  Z5V_3 = Zener Diode [part_number=1N4732A breakdown_voltage=3.6V package="300 mil [THT]"]
  10kΩ_5 = Resistor [tolerance=±5% resistance=10k power=0.25 package=THT]
  Z5V_4 = Zener Diode [part_number=1N4732A breakdown_voltage=3.6V package="300 mil [THT]"]

nets:
  N1: ATTINY45.PB5(NRES), 1kΩ.Pin_0
  N2: ATTINY45.PB3(ADC3), 10kΩ_5.Pin_1, Z5V_4.cathode
  N3: ATTINY45.PB4(ADC2), 1kΩ_2.Pin_0, 10kΩ.Pin_0
  GND: ATTINY45.GND, 7805.GND, Terminal_Block.pin6, 100nf.0, 330nf.0, 10kΩ.Pin_1, 47nf.0, Z5V.anode, Z5V_2.anode, Z5V_3.anode, Z5V_4.anode
  N4: ATTINY45.PB0(MOSI), 10kΩ_4.Pin_1, Z5V_3.cathode
  N5: ATTINY45.PB1(MISO), 10kΩ_3.Pin_1, Z5V_2.cathode
  N6: ATTINY45.PB2(SCK_ADC1), 10kΩ_2.Pin_1, Z5V.cathode
  N7: ATTINY45.VCC, 7805.OUT, 1kΩ.Pin_1, 100nf.1
  N8: 7805.IN, Terminal_Block.pin1, 330nf.1, N-FET.drain
  N9: Terminal_Block.pin2, 10kΩ_2.Pin_0
  N10: Terminal_Block.pin3, 10kΩ_3.Pin_0
  N11: Terminal_Block.pin4, 10kΩ_4.Pin_0
  N12: Terminal_Block.pin5, 10kΩ_5.Pin_0
  N13: Terminal_Block.pin7, 220Ω.Pin_1, 47nf.1
  N14: 1kΩ_2.Pin_1, N-FET.gate
  N15: 220Ω.Pin_0, N-FET.source

notes:
  12V
  GND
  OUT
  SW1
  SW2
  SW3
  SW4
  Fan Speed Controller v4.0
  ©2022 That Ain't Working
  B
